// Logisim project 2Way_Traffic_Light_Controller.circ as structural Verilog: 1 circuit, main circuit main
module main (
);

  wire and_1_out, and_2_out, clock_1_out, D0_q, D0_qn, D1_q, D1_qn, G_p1, nand_1_out, not_1_out, R_p1, R_p3,
       rgbled_1_p1, xor_1_out, Y_p3, Y_p4, Y_p5, Y_p6;

  Clock clock_1 (.out(clock_1_out));
  xor xor_1 (xor_1_out, D0_q, D1_q);
  D_Flip_Flop D0 (.D(D0_qn), .clk(clock_1_out), .Q(D0_q), .Qn(D0_qn));  // open: preset, reset
  D_Flip_Flop D1 (.D(xor_1_out), .clk(clock_1_out), .Q(D1_q), .Qn(D1_qn));  // open: preset, reset
  not not_1 (not_1_out, xor_1_out);
  and and_1 (and_1_out, D1_q, D0_q);
  nand nand_1 (nand_1_out, D1_q, D0_q);
  // RGBLED Rh: pin names not known; wires that end beside it: nand_1_out
  // RGBLED R: pin names not known; wires that end beside it: R_p1, not_1_out, R_p3, R_p3
  // RGBLED Y: pin names not known; wires that end beside it: D0_qn, D0_qn, Y_p3, Y_p4, Y_p5, Y_p6, Y_p6, Y_p3, Y_p5
  and and_2 (and_2_out, D0_q, D1_qn);
  // RGBLED G: pin names not known; wires that end beside it: G_p1, and_2_out
  // RGBLED Gh: pin names not known; wires that end beside it: and_1_out
  // RGBLED rgbled_1: pin names not known; wires that end beside it: rgbled_1_p1, rgbled_1_p1, rgbled_1_p1, rgbled_1_p1, rgbled_1_p1, rgbled_1_p1, Y_p4, G_p1
endmodule
