// Logisim project 3to8_Active_High_Decoder.circ as structural Verilog: 1 circuit, main circuit main
module main (
  input  in_1,
  input  in_2,
  input  in_3,
  output out_4,
  output out_5,
  output out_6,
  output out_7,
  output _4,
  output out_9,
  output _6,
  output _7
);

  wire not_1_out, not_2_out, not_3_out;

  not not_1 (not_1_out, in_1);
  not not_2 (not_2_out, in_2);
  not not_3 (not_3_out, in_3);
  and and_1 (out_4, not_1_out, not_2_out, not_3_out);
  and and_2 (out_5, not_1_out, not_2_out, in_3);
  and and_3 (out_6, not_1_out, in_2, not_3_out);
  and and_4 (out_7, not_1_out, in_2, in_3);
  and and_5 (_4, in_1, not_2_out, not_3_out);
  and and_6 (out_9, in_1, not_2_out, in_3);
  and and_7 (_6, in_1, in_2, not_3_out);
  and and_8 (_7, in_1, in_2, in_3);

  // Notes on the sheet:
  //   A
  //   B
  //   C
  //   0
  //   1
  //   2
  //   3
  //   5
endmodule
