// Logisim project 4Bit_Ripple_Carry_Adder.circ as structural Verilog: 2 circuits, main circuit main
module main (
  input  A,
  input  B,
  input  Cin,
  output S,
  output Cout
);

  wire and_1_out, and_2_out, xor_1_out;

  xor xor_1 (xor_1_out, B, A);
  and and_1 (and_1_out, Cin, xor_1_out);
  and and_2 (and_2_out, B, A);
  ExactlyOne xor_2 (.out(S), .in0(Cin), .in1(B), .in2(A));
  or or_1 (Cout, and_1_out, and_2_out);
endmodule

module A_4Bit_Adder (
  input  A1,
  input  A0,
  input  A3,
  input  A2,
  input  B1,
  input  B0,
  input  B3,
  input  B2,
  output out_9,
  output out_10,
  output out_11,
  output out_12,
  output out_13
);

  wire main_2_cout, main_3_cout, main_4_cout;

  main main_1 (.A(A3), .B(B3), .Cin(main_2_cout), .S(out_12), .Cout(out_11));
  main main_2 (.A(A2), .B(B2), .Cin(main_3_cout), .S(out_9), .Cout(main_2_cout));
  main main_3 (.A(A1), .B(B1), .Cin(main_4_cout), .S(out_10), .Cout(main_3_cout));
  main main_4 (.A(A0), .B(B0), .Cin(1'b0), .S(out_13), .Cout(main_4_cout));
endmodule
