// Logisim project Carry_Lookahead_Adder_4Bit.circ as structural Verilog: 1 circuit, main circuit main
module main (
  input  B3,
  input  A3,
  input  B2,
  input  A2,
  input  B0,
  input  A0,
  input  B1,
  input  A1,
  input  C0,
  output S0,
  output S1,
  output S2,
  output S3,
  output S4
);

  wire and_1_out, and_2_out, and_3_out, and_4_out, and_5_out, and_6_out, and_7_out, and_8_out, and_9_out,
       and_10_out, and_11_out, and_12_out, and_13_out, and_14_out, or_1_out, or_2_out, or_3_out, xor_1_out,
       xor_2_out, xor_3_out, xor_4_out;

  and and_1 (and_1_out, B3, A3);
  xor xor_1 (xor_1_out, B3, A3);
  and and_2 (and_2_out, B2, A2);
  xor xor_2 (xor_2_out, B2, A2);
  and and_3 (and_3_out, B1, A1);
  xor xor_3 (xor_3_out, B1, A1);
  and and_4 (and_4_out, B0, A0);
  xor xor_4 (xor_4_out, B0, A0);
  and and_5 (and_5_out, xor_4_out, C0);
  and and_6 (and_6_out, xor_4_out, xor_3_out, C0);
  and and_7 (and_7_out, and_4_out, xor_3_out);
  and and_8 (and_8_out, xor_2_out, xor_3_out, xor_4_out, C0);
  and and_9 (and_9_out, xor_2_out, xor_3_out, and_4_out);
  and and_10 (and_10_out, xor_2_out, and_3_out);
  and and_11 (and_11_out, xor_1_out, xor_2_out, xor_3_out, xor_4_out, C0);
  and and_12 (and_12_out, xor_1_out, xor_2_out, xor_3_out, and_4_out);
  and and_13 (and_13_out, xor_1_out, xor_2_out, and_4_out);
  and and_14 (and_14_out, xor_1_out, and_2_out);
  or or_1 (or_1_out, and_5_out, and_4_out);
  or or_2 (or_2_out, and_6_out, and_7_out, and_3_out);
  or or_3 (or_3_out, and_8_out, and_9_out, and_10_out, and_2_out);
  or or_4 (S4, and_11_out, and_12_out, and_13_out, and_14_out, and_1_out);
  xor xor_5 (S0, C0, xor_4_out);
  xor xor_6 (S1, or_1_out, xor_3_out);
  xor xor_7 (S2, or_2_out, xor_2_out);
  xor xor_8 (S3, or_3_out, xor_1_out);

  // Notes on the sheet:
  //   Q3
  //   P3
  //   Q2
  //   P2
  //   Q1
  //   P1
  //   Q0
  //   P0
  //   C1
  //   C2
  //   C3
  //   C4
endmodule
