// Logisim project Cascaded_8to1_Multiplexer.circ as structural Verilog: 1 circuit, main circuit main
module main (
  input  in_1,
  input  in_2,
  input  in_3,
  input  in_4,
  input  in_5,
  input  in_6,
  input  in_7,
  input  in_8,
  input  [2:0] in_9,
  input  in_10,
  input  in_11,
  input  in_12,
  input  in_13,
  input  in_14,
  input  in_15,
  input  in_16,
  input  in_17,
  input  in_18,
  output out_19
);

  wire multiplexer_1_out, multiplexer_2_out;

  Multiplexer #(.select(3)) multiplexer_1 (
    .in0(in_1), .in1(in_2), .in2(in_3), .in3(in_4), .in4(in_5), .in5(in_6), .in6(in_7), .in7(in_8),
    .out(multiplexer_1_out), .sel(in_9));
  Multiplexer #(.select(3)) multiplexer_2 (
    .in0(in_10), .in1(in_11), .in2(in_12), .in3(in_13), .in4(in_14), .in5(in_15), .in6(in_16), .in7(in_17),
    .out(multiplexer_2_out), .sel(in_9));
  Multiplexer multiplexer_3 (.in0(multiplexer_1_out), .in1(multiplexer_2_out), .out(out_19), .sel(in_18));
endmodule
