// Logisim project IC_Parity_Generator.circ as structural Verilog: 1 circuit, main circuit main
module main (
  input  A,
  input  B,
  input  C,
  input  D,
  output out_5
);

  wire n7486_1_pin1, n7486_1_pin2;

  _7486 #(.ShowInternalStructure("true")) u_7486_1 (
    .pin1(n7486_1_pin1), .pin2(n7486_1_pin2), .pin3(out_5), .pin13(A), .pin12(B), .pin11(n7486_1_pin1),
    .pin10(C), .pin9(D), .pin8(n7486_1_pin2));  // open: pin4, pin5, pin6

  // Notes on the sheet:
  //   P
endmodule
