// Logisim project JK_FlipFlop_From_D_FF.circ as structural Verilog: 1 circuit, main circuit main
module main (
  input  J,
  input  K,
  output Q,
  output Q_prime
);

  wire and_1_out, and_2_out, clock_1_out, not_1_out, or_1_out;

  not not_1 (not_1_out, K);
  and and_1 (and_1_out, Q_prime, J);
  and and_2 (and_2_out, not_1_out, Q);
  or or_1 (or_1_out, and_1_out, and_2_out);
  D_Flip_Flop d_ff_1 (.D(or_1_out), .clk(clock_1_out), .Q(Q), .Qn(Q_prime));  // open: preset, reset
  Clock clock_1 (.out(clock_1_out));

  // Notes on the sheet:
  //   Q`
  //   Q
  //   JK FF
endmodule
