// Logisim project MUX_Logic_Implementation.circ as structural Verilog: 1 circuit, main circuit main
module main (
  input  D,
  input  C,
  input  [1:0] B,
  output F
);

  wire nand_1_out, not_1_out, not_2_out, or_1_out;

  or or_1 (or_1_out, D, C);
  not not_1 (not_1_out, D);
  not not_2 (not_2_out, C);
  nand nand_1 (nand_1_out, D, C);
  Multiplexer #(.select(2)) multiplexer_1 (
    .in0(not_1_out), .in1(not_2_out), .in2(nand_1_out), .in3(or_1_out), .out(F), .sel(B));

  // Notes on the sheet:
  //   A
endmodule
