// Logisim project Master_Slave_D_FlipFlop.circ as structural Verilog: 3 circuits, main circuit main
module main (
  input  D,
  output Q
);

  wire clock_1_out, d_latch_1_q, not_1_out;

  Clock clock_1 (.out(clock_1_out));
  not not_1 (not_1_out, clock_1_out);
  D_Latch d_latch_1 (.D(D), .En(clock_1_out), .Q(d_latch_1_q));  // open: Q_prime
  D_Latch d_latch_2 (.D(d_latch_1_q), .En(not_1_out), .Q(Q));  // open: Q_prime

  // Notes on the sheet:
  //   D Latch Master
  //   D Latch Slave
endmodule

module SR_Latch (
  input  in_1,
  input  En,
  input  R,
  output Q,
  output Q_prime
);

  wire nand_1_out, nand_2_out;

  nand nand_1 (nand_1_out, in_1, En);
  nand nand_2 (nand_2_out, En, R);
  nand nand_3 (Q, nand_1_out, Q_prime);
  nand nand_4 (Q_prime, Q, nand_2_out);

  // Notes on the sheet:
  //   S
  //   SR Latch
endmodule

module D_Latch (
  input  D,
  input  En,
  output Q,
  output Q_prime
);

  wire nand_1_out, nand_2_out, not_1_out;

  not not_1 (not_1_out, D);
  nand nand_1 (nand_1_out, D, En);
  nand nand_2 (nand_2_out, En, not_1_out);
  nand nand_3 (Q, nand_1_out, Q_prime);
  nand nand_4 (Q_prime, Q, nand_2_out);

  // Notes on the sheet:
  //   D Latch
endmodule
