// Logisim project SR_Latch_NAND_Gates.circ as structural Verilog
module main (
  input  in_1,
  input  En,
  input  R,
  output Q,
  output Q_prime
);

  wire nand_1_out, nand_2_out;

  nand nand_1 (nand_1_out, in_1, En);
  nand nand_2 (nand_2_out, En, R);
  nand nand_3 (Q, nand_1_out, Q_prime);
  nand nand_4 (Q_prime, Q, nand_2_out);

  // Notes on the sheet:
  //   S
  //   SR Latch
endmodule
