// Logisim project Sequential_State_Machine_1.circ as structural Verilog: 1 circuit, main circuit main
module main (
  input  X
);

  wire A_q, A_qn, and_1_out, and_2_out, and_3_out, and_4_out, B_q, clock_1_out, not_1_out, or_1_out, or_2_out;

  not not_1 (not_1_out, X);
  and and_1 (and_1_out, B_q, X);
  and and_2 (and_2_out, A_q, not_1_out);
  and and_3 (and_3_out, A_qn, X);
  and and_4 (and_4_out, not_1_out, B_q);
  or or_1 (or_1_out, and_1_out, and_2_out);
  or or_2 (or_2_out, and_3_out, and_4_out);
  D_Flip_Flop A (.D(or_1_out), .clk(clock_1_out), .Q(A_q), .Qn(A_qn));  // open: preset, reset
  Clock clock_1 (.out(clock_1_out));
  D_Flip_Flop B (.D(or_2_out), .clk(clock_1_out), .Q(B_q));  // open: Qn, preset, reset
endmodule
