// Logisim project Sequential_State_Machine_2.circ as structural Verilog: 1 circuit, main circuit main
module main (
  input  d,
  input  n,
  output out_3
);

  wire and_1_out, and_2_out, and_3_out, and_4_out, and_5_out, and_6_out, clock_1_out, D1_q, D1_qn, D2_q,
       D2_qn, not_1_out, or_1_out, or_2_out;

  not not_1 (not_1_out, n);
  and and_1 (and_1_out, D1_q, D2_qn);
  and and_2 (and_2_out, D1_qn, d);
  and and_3 (and_3_out, D1_qn, n, D2_q);
  and and_4 (and_4_out, D2_qn, n);
  and and_5 (and_5_out, d, D2_qn, D1_q);
  and and_6 (and_6_out, D1_qn, D2_q, not_1_out);
  or or_1 (or_1_out, and_1_out, and_2_out, and_3_out);
  Clock clock_1 (.out(clock_1_out));
  or or_2 (or_2_out, and_4_out, and_5_out, and_6_out);
  D_Flip_Flop D1 (.D(or_1_out), .clk(clock_1_out), .Q(D1_q), .Qn(D1_qn));  // open: preset, reset
  D_Flip_Flop D2 (.D(or_2_out), .clk(clock_1_out), .Q(D2_q), .Qn(D2_qn));  // open: preset, reset
  and and_7 (out_3, D1_q, D2_q);
endmodule
