// Logisim project Smart_4Way_Traffic_Light.circ as structural Verilog: 1 circuit, main circuit main
module main (
);

  wire and_1_out, and_2_out, and_3_out, and_4_out, and_5_out, and_6_out, and_7_out, and_8_out, and_9_out,
       and_10_out, clock_1_out, D1_q, D1_qn, D2_q, D2_qn, D3_q, D3_qn, or_1_out, or_2_out, or_3_out, Re_p1,
       Rn_p2;

  and and_1 (and_1_out, D2_q, D3_q);
  and and_2 (and_2_out, D3_qn, D1_q);
  and and_3 (and_3_out, D2_q, D3_qn);
  and and_4 (and_4_out, D3_q, D1_qn, D2_qn);
  or or_1 (or_1_out, and_1_out, and_2_out);
  Clock clock_1 (.out(clock_1_out));
  or or_2 (or_2_out, and_3_out, and_4_out);
  D_Flip_Flop D1 (.D(or_1_out), .clk(clock_1_out), .Q(D1_q), .Qn(D1_qn));  // open: preset, reset
  D_Flip_Flop D2 (.D(or_2_out), .clk(clock_1_out), .Q(D2_q), .Qn(D2_qn));  // open: preset, reset
  D_Flip_Flop D3 (.D(D3_qn), .clk(clock_1_out), .Q(D3_q), .Qn(D3_qn));  // open: preset, reset
  and and_5 (and_5_out, D3_qn, D1_q);
  and and_6 (and_6_out, D3_q, D1_qn);
  or or_3 (or_3_out, and_5_out, and_6_out, D2_q);
  and and_7 (and_7_out, D2_qn, D3_qn);
  and and_8 (and_8_out, D1_q, D3_q);
  and and_9 (and_9_out, D1_qn, D3_q);
  and and_10 (and_10_out, D2_q, D3_qn);
  // RGBLED Rn: pin names not known; wires that end beside it: or_3_out, Rn_p2
  // RGBLED Yn: pin names not known; wires that end beside it: and_7_out, and_7_out
  // RGBLED Gn: pin names not known
  // RGBLED Re: pin names not known; wires that end beside it: Re_p1, D2_qn
  // RGBLED Ye: pin names not known; wires that end beside it: and_9_out, and_9_out
  // RGBLED De: pin names not known; wires that end beside it: Rn_p2
  // RGBLED Rs: pin names not known; wires that end beside it: or_3_out
  // RGBLED Ys: pin names not known; wires that end beside it: and_7_out
  // RGBLED Gs: pin names not known; wires that end beside it: and_8_out, Re_p1
  // RGBLED Rw: pin names not known; wires that end beside it: D2_qn
  // RGBLED Yw: pin names not known; wires that end beside it: and_9_out, and_9_out
  // RGBLED Gw: pin names not known; wires that end beside it: and_10_out

  // Notes on the sheet:
  //   North
  //   East
  //   South
  //   West
endmodule
