// Logisim project Project.circ as structural Verilog: 1 circuit, main circuit main
module main (
);

  wire and_1_out, and_2_out, and_3_out, and_4_out, and_5_out, and_6_out, and_7_out, and_8_out, and_9_out,
       and_10_out, and_11_out, and_12_out, and_13_out, and_14_out, and_15_out, and_16_out, and_17_out,
       and_18_out, and_19_out, and_20_out, and_21_out, and_22_out, and_23_out, and_24_out, and_25_out,
       and_26_out, and_27_out, and_28_out, and_29_out, and_30_out, and_31_out, and_32_out, and_33_out,
       and_34_out, and_35_out, and_36_out, and_37_out, and_38_out, and_39_out, and_40_out, and_41_out,
       clock_1_out, not_1_out, not_2_out, or_1_out, or_2_out, or_3_out, or_4_out, or_5_out, or_6_out,
       or_7_out, or_8_out, or_9_out, or_10_out, or_11_out, or_12_out, or_13_out, or_14_out, or_15_out,
       or_16_out, or_17_out, or_18_out, or_19_out, or_20_out, or_21_out, or_22_out, or_23_out, or_24_out,
       or_25_out, Q0_q, Q0_qn, Q1_q, Q1_qn, Q2_q, Q2_qn, Q3_q, Q3_qn, rgbled_28_p2, rgbled_31_p1, xor_1_out;

  and and_1 (and_1_out, Q0_qn, Q1_q, Q2_q, Q3_q);
  and and_2 (and_2_out, Q0_q, Q1_qn);
  and and_3 (and_3_out, Q0_q, Q2_qn);
  and and_4 (and_4_out, Q0_q, Q3_qn);
  and and_5 (and_5_out, Q1_q, Q2_qn);
  and and_6 (and_6_out, Q1_q, Q3_qn);
  and and_7 (and_7_out, Q3_q, Q2_q, Q1_qn);
  Clock clock_1 (.out(clock_1_out));
  or or_1 (or_1_out, and_1_out, and_2_out, and_3_out, and_4_out);
  or or_2 (or_2_out, and_5_out, and_6_out, and_7_out);
  xor xor_1 (xor_1_out, Q2_q, Q3_q);
  D_Flip_Flop Q0 (.D(or_1_out), .clk(clock_1_out), .Q(Q0_q), .Qn(Q0_qn));  // open: preset, reset
  D_Flip_Flop Q1 (.D(or_2_out), .clk(clock_1_out), .Q(Q1_q), .Qn(Q1_qn));  // open: preset, reset
  D_Flip_Flop Q2 (.D(xor_1_out), .clk(clock_1_out), .Q(Q2_q), .Qn(Q2_qn));  // open: preset, reset
  D_Flip_Flop Q3 (.D(Q3_qn), .clk(clock_1_out), .Q(Q3_q), .Qn(Q3_qn));  // open: preset, reset
  and and_8 (and_8_out, Q2_q, Q3_q);
  and and_9 (and_9_out, Q0_qn, Q1_qn, Q2_qn, Q3_qn);
  and and_10 (and_10_out, Q0_qn, Q1_qn, Q2_q, Q3_qn);
  and and_11 (and_11_out, Q0_qn, Q1_q, Q2_qn, Q3_qn);
  and and_12 (and_12_out, Q0_qn, Q1_q, Q2_q, Q3_qn);
  and and_13 (and_13_out, Q3_q, Q2_q);
  or or_3 (or_3_out, Q0_q, Q1_q);
  or or_4 (or_4_out, Q0_q, Q1_q, and_8_out);
  or or_5 (or_5_out, and_9_out, and_10_out);
  and and_14 (and_14_out, Q0_qn, Q1_qn, Q2_qn, Q3_q);
  and and_15 (and_15_out, Q2_q, Q3_q);
  and and_16 (and_16_out, Q2_q, Q3_q);
  and and_17 (and_17_out, Q0_q, Q1_qn, Q2_qn, Q3_qn);
  and and_18 (and_18_out, Q0_q, Q1_qn, Q2_q, Q3_qn);
  and and_19 (and_19_out, Q0_q, Q1_q, Q2_qn, Q3_qn);
  and and_20 (and_20_out, Q0_q, Q1_q, Q2_q, Q3_qn);
  or or_6 (or_6_out, and_11_out, and_12_out);
  and and_21 (and_21_out, Q0_qn, Q1_q, Q2_qn, Q3_q);
  or or_7 (or_7_out, and_16_out, Q0_qn, Q1_q);
  or or_8 (or_8_out, and_17_out, and_18_out);
  and and_22 (and_22_out, Q0_q, Q1_qn, Q2_qn, Q3_q);
  or or_9 (or_9_out, and_13_out, Q1_qn, Q0_qn);
  or or_10 (or_10_out, and_19_out, and_20_out);
  and and_23 (and_23_out, Q0_q, Q1_q, Q2_qn, Q3_q);
  or or_11 (or_11_out, and_15_out, Q1_qn, Q0_q);
  and and_24 (and_24_out, Q0_qn, Q1_qn, Q2_qn, Q3_qn);
  and and_25 (and_25_out, Q0_qn, Q1_qn, Q2_q, Q3_q);
  and and_26 (and_26_out, Q0_qn, Q1_qn, Q2_qn, Q3_q);
  and and_27 (and_27_out, Q0_qn, Q1_qn, Q2_q, Q3_qn);
  // RGBLED rgbled_1: pin names not known; wires that end beside it: or_4_out
  // RGBLED rgbled_2: pin names not known; wires that end beside it: or_5_out, or_5_out
  // RGBLED rgbled_3: pin names not known; wires that end beside it: and_14_out
  // RGBLED rgbled_4: pin names not known; wires that end beside it: or_11_out
  // RGBLED rgbled_5: pin names not known; wires that end beside it: or_6_out
  // RGBLED rgbled_6: pin names not known; wires that end beside it: and_21_out
  // RGBLED rgbled_7: pin names not known; wires that end beside it: or_7_out
  // RGBLED rgbled_8: pin names not known; wires that end beside it: or_8_out
  // RGBLED rgbled_9: pin names not known; wires that end beside it: and_22_out
  // RGBLED rgbled_10: pin names not known; wires that end beside it: or_9_out
  // RGBLED rgbled_11: pin names not known; wires that end beside it: or_10_out
  // RGBLED rgbled_12: pin names not known; wires that end beside it: and_23_out
  or or_12 (or_12_out, and_24_out, and_25_out);
  or or_13 (or_13_out, and_26_out, and_27_out);
  not not_1 (not_1_out, Q0_q);
  and and_28 (and_28_out, not_1_out, Q2_qn, Q1_q, Q3_qn);
  and and_29 (and_29_out, not_1_out, Q1_q, Q2_q, Q3_q);
  and and_30 (and_30_out, Q0_qn, Q1_q, Q2_qn, Q3_q);
  and and_31 (and_31_out, Q0_qn, Q1_q, Q2_q, Q3_qn);
  and and_32 (and_32_out, Q0_q, Q1_qn, Q2_qn, Q3_q);
  and and_33 (and_33_out, Q0_q, Q1_qn, Q2_q, Q3_qn);
  and and_34 (and_34_out, Q1_qn, Q0_q, Q2_qn, Q3_qn);
  and and_35 (and_35_out, Q1_qn, Q0_q, Q2_q, Q3_q);
  and and_36 (and_36_out, Q0_q, Q1_q, Q2_qn, Q3_qn);
  and and_37 (and_37_out, Q0_q, Q1_q, Q2_q, Q3_q);
  and and_38 (and_38_out, Q0_q, Q1_q, Q2_qn, Q3_q);
  and and_39 (and_39_out, Q0_q, Q1_q, Q2_q, Q3_qn);
  or or_14 (or_14_out, Q1_qn, Q0_q);
  or or_15 (or_15_out, and_28_out, and_29_out);
  or or_16 (or_16_out, and_30_out, and_31_out);
  or or_17 (or_17_out, Q0_qn, Q1_q);
  or or_18 (or_18_out, and_32_out, and_33_out);
  or or_19 (or_19_out, Q0_qn, Q1_qn);
  or or_20 (or_20_out, and_34_out, and_35_out);
  or or_21 (or_21_out, and_36_out, and_37_out);
  or or_22 (or_22_out, and_38_out, and_39_out);
  // RGBLED rgbled_13: pin names not known; wires that end beside it: or_3_out
  // RGBLED rgbled_14: pin names not known; wires that end beside it: or_12_out
  // RGBLED rgbled_15: pin names not known; wires that end beside it: or_13_out
  // RGBLED rgbled_16: pin names not known; wires that end beside it: or_14_out
  // RGBLED rgbled_17: pin names not known; wires that end beside it: or_15_out
  // RGBLED rgbled_18: pin names not known; wires that end beside it: or_16_out
  // RGBLED rgbled_19: pin names not known; wires that end beside it: or_17_out
  // RGBLED rgbled_20: pin names not known; wires that end beside it: or_20_out
  // RGBLED rgbled_21: pin names not known; wires that end beside it: or_18_out
  // RGBLED rgbled_22: pin names not known; wires that end beside it: or_19_out
  // RGBLED rgbled_23: pin names not known; wires that end beside it: or_21_out
  // RGBLED rgbled_24: pin names not known; wires that end beside it: or_22_out
  or or_23 (or_23_out, Q2_qn, Q3_q);
  not not_2 (not_2_out, or_23_out);
  LED led_1 (.in(not_2_out));
  LED led_2 (.in(or_23_out));
  LED led_3 (.in(not_2_out));
  LED led_4 (.in(or_23_out));
  LED led_5 (.in(not_2_out));
  LED led_6 (.in(or_23_out));
  LED led_7 (.in(not_2_out));
  LED led_8 (.in(or_23_out));
  or or_24 (or_24_out, Q1_qn, Q2_qn, Q3_q);
  and and_40 (and_40_out, Q1_q, Q2_q, Q3_qn);
  or or_25 (or_25_out, Q3_q, Q1_q, Q2_qn);
  and and_41 (and_41_out, Q1_qn, Q2_q, Q3_qn);
  // RGBLED rgbled_25: pin names not known; wires that end beside it: or_24_out
  // RGBLED rgbled_26: pin names not known; wires that end beside it: and_40_out
  // RGBLED rgbled_27: pin names not known; wires that end beside it: or_25_out
  // RGBLED rgbled_28: pin names not known; wires that end beside it: and_41_out, rgbled_28_p2, rgbled_28_p2
  // RGBLED rgbled_29: pin names not known; wires that end beside it: or_24_out
  // RGBLED rgbled_30: pin names not known; wires that end beside it: and_40_out
  // RGBLED rgbled_31: pin names not known; wires that end beside it: rgbled_31_p1, or_25_out
  // RGBLED rgbled_32: pin names not known; wires that end beside it: and_41_out

  // Notes on the sheet:
  //   Q0
  //   q0`
  //   Q1
  //   Q1`
  //   Q2
  //   Q2`
  //   North
  //   Q3
  //   Q3`
  //   North left
  //   East left
  //   South Left
  //   West left
  //   North
  //   East
  //   South
  //   West
  //   North right
  //   East right
  //   Souht right 
  //   West Right
  //   Human North
  //   Human East
  //   Human South
  //   Human West
endmodule
